# Fritzing sketch Soundhunter_Fritzing (saved by Fritzing 1.0.6)
breadboards: 1

parts:
  U1 = LuaNode32 / ESP32 [part_number=ESP32S-PIN30]
  OLED_I2C1 = OLED 128x64 I2C Monochrome Display
  Part1 = Adafruit MAX4466 Electret Microphone Amplifier [part_number="Adafruit #1063"]
  Part2 = Adafruit MAX4466 Electret Microphone Amplifier [part_number="Adafruit #1063"]
  Part3 = Adafruit MAX4466 Electret Microphone Amplifier [part_number="Adafruit #1063"]
  Part4 = Adafruit MAX4466 Electret Microphone Amplifier [part_number="Adafruit #1063"]

nets:
  N1: U1.D34, Part2.OUT, Part3.OUT
  N2: U1.D32, Part1.OUT
  N3: U1.D33, Part4.OUT
  GND: U1.GND, Part1.GND, Part2.GND, Part4.GND
  VCC: U1.3V3, Part1.VCC, Part2.VCC, Part4.VCC
  N4: U1.D19, OLED_I2C1.SDA
  N5: U1.D22, OLED_I2C1.SCK
  VDD: OLED_I2C1.VDD, Part3.VCC
  GND_2: OLED_I2C1.GND, Part3.GND

custom parts:
  LuaNode32 / ESP32: New Image for LuaNode32 DOIT ESP32 DEVKIT V1. Base parts from LuaNode32 / ESP32 ESP32 based LuaNode32 by G.Noorlander DOIT Esp32 DevKit v1 (30 pins long, 11 pins width) by Werner Rothschopf (modified by vanepp Dec 2018)
  Adafruit MAX4466 Electret Microphone Amplifier: Add an ear to your project with this well-designed electret microphone amplifier. This fully assembled and tested board comes with a 20-20KHz electret microphone soldered on. For the amplification, we use the Maxim MAX4466, an op-amp specifically designed for this delicate task! The amplifier has excellent power supply noise rejection, so this amplifier sounds really good and isn't nearly as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
